# Fritzing sketch bitbot (saved by Fritzing 0.9.1b)
circuit board: 8.46667cm x 5.64444cm
breadboards: 2
perfboards: 1

parts:
  Onderdeel1 = Arduino Uno (Rev3)
  LED4 = LED - 5mm [color="Red (633nm)" package="5 mm [THT]"]
  LED5 = LED - 5mm [color="Red (633nm)" package="5 mm [THT]"]
  LED6 = LED - 5mm [color="Red (633nm)" package="5 mm [THT]"]
  LED7 = LED - 5mm [color="Red (633nm)" package="5 mm [THT]"]
  LED8 = LED - 5mm [color="Red (633nm)" package="5 mm [THT]"]
  LED9 = LED - 5mm [color="Red (633nm)" package="5 mm [THT]"]
  R1 = Resistor [tolerance=±5% resistance=10k package="0603 [SMD]"]
  R2 = Resistor [tolerance=±5% resistance=10k package="0603 [SMD]"]
  R3 = Resistor [tolerance=±5% resistance=10k package="0603 [SMD]"]
  R4 = Resistor [tolerance=±5% resistance=10k package="0603 [SMD]"]
  R5 = Resistor [tolerance=±5% resistance=10k package="0603 [SMD]"]
  R6 = Resistor [tolerance=±5% resistance=10k package="0603 [SMD]"]
  R7 = Resistor [tolerance=±5% resistance=10k package="0603 [SMD]"]
  R8 = Resistor [tolerance=±5% resistance=10k package="0603 [SMD]"]
  LED3 = LED - 5mm [color="Red (633nm)" package="5 mm [THT]"]
  LED2 = LED - 5mm [color="Red (633nm)" package="5 mm [THT]"]
  J1 = Piezo Speaker
  R9 = Temperature Sensor (Thermistor) [thermistor_type=NTC package=THT]
  R10 = PHOTOCELL [package=photocell-kit]
  R11 = Resistor [tolerance=±5% resistance=10k package="0603 [SMD]"]
  R12 = Resistor [tolerance=±5% resistance=10k package="0603 [SMD]"]
  J2 = Basic Servo [part_number=Links]
  J3 = Basic Servo [part_number=Rechts]
  S1 = Round Pushbutton
  S2 = Round Pushbutton
  R13 = Resistor [tolerance=±5% resistance=10k package="0603 [SMD]"]
  R14 = Resistor [tolerance=±5% resistance=222 package="0603 [SMD]"]
  Onderdeel2 = LED Matrix - Serial Interface - Red/Green/Blue
  Onderdeel3 = LSM303 Breakout Board - Tilt-Compensated Compass

nets:
  5V: Onderdeel1.A1, Onderdeel1.5V, R11.Pin_1, R12.Pin_1, Onderdeel2.VCC, Onderdeel2.SCK, Onderdeel3.SCL_M
  N1: Onderdeel1.A4/SDA, Onderdeel2.MISO, Onderdeel3.DRDY
  N2: Onderdeel1.A5/SCL, Onderdeel2.GND, Onderdeel3.SA0
  N3: Onderdeel1.D8, R3.Pin_1
  N4: Onderdeel1.D9_PWM, R7.Pin_0
  N5: Onderdeel1.D10_PWM/SS, J1.pin2
  N6: Onderdeel1.D11_PWM/MOSI, R14.Pin_1
  N7: Onderdeel1.D12/MISO, J2.pulse
  N8: Onderdeel1.D13/SCK, J3.pulse
  N9: Onderdeel1.GND, LED4.cathode, LED5.cathode, LED6.cathode, LED7.cathode, LED8.cathode, LED9.cathode, LED3.cathode, LED2.cathode, J1.pin1, R9.pin_1, R10.P$2, Onderdeel2.CS, Onderdeel3.SDA_M
  N10: Onderdeel1.D2, R4.Pin_0
  N11: Onderdeel1.D3_PWM, R5.Pin_0
  N12: Onderdeel1.D4, R6.Pin_0
  N13: Onderdeel1.D5_PWM, R8.Pin_1
  N14: Onderdeel1.D6_PWM, R1.Pin_1
  N15: Onderdeel1.D7, R2.Pin_1
  N16: LED4.anode, R4.Pin_1
  N17: LED5.anode, R5.Pin_1
  N18: LED6.anode, R6.Pin_1
  N19: LED7.anode, R2.Pin_0
  N20: LED8.anode, R1.Pin_0
  N21: LED9.anode, R8.Pin_0
  N22: R3.Pin_0, LED3.anode
  N23: R7.Pin_1, LED2.anode
  N24: R9.pin_0, R12.Pin_0
  N25: R10.P$1, R11.Pin_0
  GND: J2.gnd, J3.gnd, S1.leg1, S2.leg1
  VCC: J2.vcc, J3.vcc, R13.Pin_1
  N26: S1.leg0, S2.leg0, R13.Pin_0, R14.Pin_0

notes:
  voelsprieten
